# Fritzing sketch Stazione Meteo (saved by Fritzing 0.8.3b)

parts:
  Componente1 = Arduino Uno (Rev3)  # not connected
  Componente2 = Arduino Ethernet Shield (Rev3)
  RHT1 = Humidity and Temperature Sensor RHT03
  Componente3 = Barometric Pressure Sensor - BMP085 Breakout
  Componente4 = Ambient Light Sensor (TEMT6000 Breakout Board)
  Componente5 = SRF05 Ultrasonic Rangefinder

nets:
  N1: Componente2.SPI/D12, Componente5.Trig
  N2: Componente2.SPI/D13, Componente5.Echo
  N3: Componente2.A0, Componente4.S
  N4: Componente2.A4/SDA, Componente3.SDA
  N5: Componente2.A5/SCL, Componente3.SCL
  N6: Componente2.D2, RHT1.Data-signal
  VCC: Componente2.5V, RHT1.Vcc, Componente5.VCC
  N7: Componente2.GND, RHT1.GND_2

notes:
  Sensore umidità e temperatura DHT22
  Sensore pressione e temperatura BMP085
  Sensore luminosità
  Sensore ultrasuoni HC-SR04
  Arduino UNO e Ethernet Shield
